# Fritzing sketch Sketch (saved by Fritzing 0.9.2b)

parts:
  Componente1 = LinkIt ONE
  PWM1 = PCA9685 16x12-bit PWM Breakout
  Squix1 = OLED 0.96" 128x64 I2C SSD1306
  BATT1 = LiPoly Battery (1300mAh)
  UBEC1 = UBEC
  J1 = Basic Servo

nets:
  N1: Componente1.SDA, PWM1.no_name_yet#504, PWM1.no_name_yet#604, Squix1.SCA
  N2: Componente1.SCL, PWM1.no_name_yet#503, PWM1.no_name_yet#603, Squix1.SCL
  5V: Componente1.5V, PWM1.no_name_yet#505, PWM1.no_name_yet#605, Squix1.VCC
  GND: Componente1.GND, PWM1.no_name_yet#501, PWM1.no_name_yet#601, PWM1.no_name_yet#701, PWM1.no_name_yet#1000, Squix1.GND, UBEC1.negative-out
  N3: PWM1.no_name_yet#0, J1.pulse
  N4: PWM1.no_name_yet#100, PWM1.no_name_yet#706, UBEC1.positive-out
  N5: BATT1.positive, UBEC1.positive-in
  N6: BATT1.negative, UBEC1.negative-in

custom parts:
  LinkIt ONE: All-in-one development board with GSM/GPRS, Bluetooth 2.0/4.0, Wi-Fi, GPS. Compatible to Arduino IDE.
  LiPoly Battery (1300mAh): Lithium Ion Polymer Battery (1300mAh)
  UBEC: UBEC - Voltage Regulator
